// Digital circuit MUX.dig as structural Verilog
module MUX (
  input  [1:0] in_1,
  input  in_2,
  output [3:0] out_3
);

  wire [3:1] undriven, undriven_2;

  Multiplexer #(.Bits(4), .Selector_Bits(2)) multiplexer_1 (
    .sel(in_1), .in_0({undriven_2, 1'b0}), .in_1({undriven, 1'b1}), .in_2({undriven, 1'b1}),
    .in_3({undriven_2, 1'b0}), .out(out_3));
  // Pins of 1 and 2 bits meet at in_1
  // Pins of 1 and 4 bits meet at {undriven_2, 1'b0}
  // Pins of 1 and 4 bits meet at {undriven, 1'b1}
  // Pins of 1 and 4 bits meet at out_3
endmodule
